// Logisim project RSC.circ as structural Verilog: 10 circuits, main circuit Arith_U
module Arith_U (
  input  [31:0] A,
  input  [31:0] in_2,
  input  [31:0] B,
  input  S1,
  input  S0,
  output [31:0] AU_out
);

  wire and_1_out, not_2_out, xor_1_out;
  wire [31:0] adder_1_out, multiplexer_1_out, not_1_out;

  assign not_1_out = ~B;  // NOT_Gate not_1, 32 bits wide
  Multiplexer #(.select(2), .width(32)) multiplexer_1 (
    .in0(not_1_out), .in1(B), .in2(in_2), .in3(B), .out(multiplexer_1_out), .sel({S1, S0}));
  not not_2 (not_2_out, xor_1_out);
  Adder #(.width(32)) adder_1 (.a(A), .b(multiplexer_1_out), .out(adder_1_out), .cin(not_2_out));  // open: cout
  Multiplexer #(.width(32)) multiplexer_2 (.in0(adder_1_out), .in1(B), .out(AU_out), .sel(and_1_out));
  and and_1 (and_1_out, S0, S1);
  xor xor_1 (xor_1_out, S1, S0);
endmodule

module Logic_U (
  input  [31:0] A,
  input  [31:0] B,
  input  S1,
  input  S0,
  output [31:0] Logic_Out
);

  wire [31:0] and_1_out, not_1_out, or_1_out, shifter_1_out;

  Shifter #(.shift("ar"), .width(32)) shifter_1 (.in(A), .\dist (5'b00001), .out(shifter_1_out));
  assign not_1_out = ~A;  // NOT_Gate not_1, 32 bits wide
  assign and_1_out = A & B;  // AND_Gate and_1, 32 bits wide
  assign or_1_out = A | B;  // OR_Gate or_1, 32 bits wide
  Multiplexer #(.select(2), .width(32)) multiplexer_1 (
    .in0(and_1_out), .in1(or_1_out), .in2(shifter_1_out), .in3(not_1_out), .out(Logic_Out), .sel({S1, S0}));
endmodule

module ALU (
  input  [31:0] A,
  input  [31:0] B,
  input  S2,
  input  S1,
  input  S0,
  output [31:0] ALU_Out
);

  wire [31:0] arith_u_1_au_out, logic_u_1_logic_out;

  Arith_U arith_u_1 (.A(A), .in_2(32'h1), .B(B), .S1(S1), .S0(S0), .AU_out(arith_u_1_au_out));
  Logic_U logic_u_1 (.A(A), .B(B), .S1(S1), .S0(S0), .Logic_Out(logic_u_1_logic_out));
  Multiplexer #(.width(32)) multiplexer_1 (.in0(arith_u_1_au_out), .in1(logic_u_1_logic_out), .out(ALU_Out), .sel(S2));
endmodule

module SC (
  input  Clock,
  input  Clear,
  output [2:0] SEQ_out
);

  wire [2:0] adder_1_out;

  Adder #(.width(3)) adder_1 (.a(SEQ_out), .b(3'b001), .out(adder_1_out));  // open: cin, cout
  Register #(.width(3)) register_1 (.D(adder_1_out), .clk(Clock), .Q(SEQ_out), .clr(Clear));  // open: en
endmodule

module DecoderCircuit (
  input  [31:0] IR_In,
  output [15:0] D_Out,
  output [3:0] Debug_Instruction
);

  wire comparator_1_gt;
  wire [15:0] decoder_1_out0;

  Comparator #(.width(28)) comparator_1 (.a(IR_In[31:4]), .b({28{1'b0}}), .gt(comparator_1_gt));  // open: eq, lt
  Decoder #(.select(4)) decoder_1 (
    .out0(decoder_1_out0[0]), .out1(decoder_1_out0[1]), .out2(decoder_1_out0[2]), .out3(decoder_1_out0[3]),
    .out4(decoder_1_out0[4]), .out5(decoder_1_out0[5]), .out6(decoder_1_out0[6]), .out7(decoder_1_out0[7]),
    .out8(decoder_1_out0[8]), .out9(decoder_1_out0[9]), .out10(decoder_1_out0[10]),
    .out11(decoder_1_out0[11]), .out12(decoder_1_out0[12]), .out13(decoder_1_out0[13]),
    .out14(decoder_1_out0[14]), .out15(decoder_1_out0[15]), .sel(IR_In[3:0]));  // open: en
  Multiplexer #(.width(16)) multiplexer_1 (.in0(decoder_1_out0), .in1({16{1'b0}}), .out(D_Out), .sel(comparator_1_gt));

  assign Debug_Instruction = IR_In[3:0];
endmodule

module TimerCircuit (
  input  Clock,
  input  Clear,
  input  Stop,
  output [7:0] T_Out
);

  wire [2:0] sc_1_seq_out;
  wire [7:0] decoder_1_out0;

  SC sc_1 (.Clock(Clock), .Clear(Clear), .SEQ_out(sc_1_seq_out));
  Decoder #(.select(3)) decoder_1 (
    .out0(decoder_1_out0[0]), .out1(decoder_1_out0[1]), .out2(decoder_1_out0[2]), .out3(decoder_1_out0[3]),
    .out4(decoder_1_out0[4]), .out5(decoder_1_out0[5]), .out6(decoder_1_out0[6]), .out7(decoder_1_out0[7]),
    .sel(sc_1_seq_out));  // open: en
  Multiplexer #(.width(8)) multiplexer_1 (.in0(decoder_1_out0), .out(T_Out), .sel(Stop));  // open: in1
endmodule

module RSC (
  output [7:0] T,
  output [3:0] D
);

  wire control_1_acc_bus, control_1_acc_clr, control_1_acc_ld, control_1_ar_ld, control_1_dr_bus,
       control_1_dr_ld, control_1_ir_ld, control_1_outr_ld, control_1_pc_bus, control_1_pc_inc,
       control_1_pc_ld, control_1_r_bus, control_1_r_ld, control_1_ram_oe, control_1_ram_we, control_1_z_ldd,
       dr_1_p6, pc_1_p5, Primary_Clock_out, r_1_p5, z_reg_1_z_out;
  wire [2:0] control_1_alu_s;
  wire [15:0] undriven;
  wire [31:0] acc_1_p2, alu_1_alu_out, ar_1_p1, ir_1_p5, outr_1_p4;

  Z_Reg z_reg_1 (.Clock(Primary_Clock_out), .Load(control_1_z_ldd), .ACC_in(acc_1_p2), .Z_out(z_reg_1_z_out));
  Control control_1 (
    .Z_In(z_reg_1_z_out), .Clk(Primary_Clock_out), .IR_In(ir_1_p5), .T(T), .IR_LD(control_1_ir_ld),
    .RAM_WE(control_1_ram_we), .D(D), .RAM_OE(control_1_ram_oe), .AR_LD(control_1_ar_ld),
    .PC_LD(control_1_pc_ld), .PC_INC(control_1_pc_inc), .PC_BUS(control_1_pc_bus), .DR_LD(control_1_dr_ld),
    .DR_BUS(control_1_dr_bus), .R_LD(control_1_r_ld), .R_BUS(control_1_r_bus), .ACC_LD(control_1_acc_ld),
    .ACC_CLR(control_1_acc_clr), .ACC_BUS(control_1_acc_bus), .ALU_S(control_1_alu_s),
    .OUTR_LD(control_1_outr_ld), .Z_lDD(control_1_z_ldd));
  Clock Primary_Clock (.out(Primary_Clock_out));
  // AR ar_1: pin names not known; wires that end beside it: ar_1_p1, control_1_ar_ld, Primary_Clock_out
  // PC pc_1: pin names not known; wires that end beside it: ar_1_p1, control_1_pc_ld, control_1_pc_inc, Primary_Clock_out, pc_1_p5, ar_1_p1
  // DR dr_1: pin names not known; wires that end beside it: control_1_pc_bus, ar_1_p1, Primary_Clock_out, control_1_dr_ld, control_1_dr_bus, dr_1_p6, ar_1_p1
  // R r_1: pin names not known; wires that end beside it: ar_1_p1, Primary_Clock_out, control_1_r_ld, control_1_r_bus, r_1_p5, ar_1_p1
  ALU alu_1 (
    .A(acc_1_p2), .B(ar_1_p1), .S2(control_1_alu_s[2]), .S1(control_1_alu_s[1]), .S0(control_1_alu_s[0]),
    .ALU_Out(alu_1_alu_out));
  // OUTR outr_1: pin names not known; wires that end beside it: ar_1_p1, control_1_outr_ld, Primary_Clock_out, outr_1_p4, Primary_Clock_out, control_1_acc_clr, control_1_acc_ld, control_1_acc_bus
  // Probe on undriven
  RAM #(.addrWidth(16), .dataWidth(32), .databus("bidir"), .trigger("high")) ram_1 (
    .addr(undriven), .we(control_1_ram_we), .oe(control_1_ram_oe), .data(ar_1_p1));
  Hex_Digit_Display #(.decimalPoint("false")) hex_digit_display_1 (.value(outr_1_p4[31:28]));
  Hex_Digit_Display #(.decimalPoint("false")) hex_digit_display_2 (.value(outr_1_p4[27:24]));
  // Probe on r_1_p5
  Hex_Digit_Display #(.decimalPoint("false")) hex_digit_display_3 (.value(outr_1_p4[23:20]));
  Hex_Digit_Display #(.decimalPoint("false")) hex_digit_display_4 (.value(outr_1_p4[19:16]));
  Hex_Digit_Display #(.decimalPoint("false")) hex_digit_display_5 (.value(outr_1_p4[15:12]));
  Hex_Digit_Display #(.decimalPoint("false")) hex_digit_display_6 (.value(outr_1_p4[11:8]));
  // ACC acc_1: pin names not known; wires that end beside it: alu_1_alu_out, acc_1_p2, ar_1_p1
  Hex_Digit_Display #(.decimalPoint("false")) hex_digit_display_7 (.value(outr_1_p4[7:4]));
  Hex_Digit_Display #(.decimalPoint("false")) hex_digit_display_8 (.value(outr_1_p4[3:0]));
  // IR ir_1: pin names not known; wires that end beside it: dr_1_p6, control_1_ir_ld, Primary_Clock_out, ar_1_p1, ir_1_p5
  // Probe on pc_1_p5
  // Probe on dr_1_p6
  // Probe on ar_1_p1
  // Probe on acc_1_p2
endmodule

module Z_Reg (
  input  Clock,
  input  Load,
  input  [31:0] ACC_in,
  output Z_out
);

  wire not_1_out, or_4_out;
  wire [3:0] or_3_out;
  wire [7:0] or_2_out;
  wire [15:0] or_1_out;

  assign or_1_out = ACC_in[15:0] | ACC_in[31:16];  // OR_Gate or_1, 16 bits wide
  assign or_2_out = or_1_out[7:0] | or_1_out[15:8];  // OR_Gate or_2, 8 bits wide
  assign or_3_out = or_2_out[3:0] | or_2_out[7:4];  // OR_Gate or_3, 4 bits wide
  or or_4 (or_4_out, or_3_out[0], or_3_out[1], or_3_out[2], or_3_out[3]);
  not not_1 (not_1_out, or_4_out);
  // Onebit_reg onebit_reg_1: pin names not known; wires that end beside it: Clock, not_1_out, 1'b0, Load, Z_out
endmodule

module Control (
  input  Z_In,
  input  Clk,
  input  [31:0] IR_In,
  output [7:0] T,
  output IR_LD,
  output RAM_WE,
  output [3:0] D,
  output RAM_OE,
  output AR_LD,
  output PC_LD,
  output PC_INC,
  output PC_BUS,
  output DR_LD,
  output DR_BUS,
  output R_LD,
  output R_BUS,
  output ACC_LD,
  output ACC_CLR,
  output ACC_BUS,
  output [2:0] ALU_S,
  output OUTR_LD,
  output Z_lDD
);

  wire pld_s_ld_1_p4, pld_sc_clr_1_p7, s_reg_1_d_out;
  wire [15:0] pld_s_ld_1_p2;

  // PLD_S_LD pld_s_ld_1: pin names not known; wires that end beside it: T[3], pld_s_ld_1_p2[0], Clk, pld_s_ld_1_p4, T[5], T[7]
  S_Reg s_reg_1 (.Clk(Clk), .Data(1'b1), .Load(pld_s_ld_1_p4), .D_Out(s_reg_1_d_out));  // open: Clear
  // PLD_SC_CLR pld_sc_clr_1: pin names not known; wires that end beside it: T[3], pld_s_ld_1_p2[1], pld_s_ld_1_p2[2], pld_s_ld_1_p2[5], pld_s_ld_1_p2[6], Z_In, pld_sc_clr_1_p7
  TimerCircuit timercircuit_1 (.Clock(Clk), .Clear(pld_sc_clr_1_p7), .Stop(s_reg_1_d_out), .T_Out(T));
  DecoderCircuit decodercircuit_1 (.IR_In(IR_In), .D_Out(pld_s_ld_1_p2), .Debug_Instruction(D));
  // PLD_IR_LD pld_ir_ld_1: pin names not known; wires that end beside it: T[2], Clk, IR_LD
  // PLD_RAM_WE pld_ram_we_1: pin names not known; wires that end beside it: T[6], pld_s_ld_1_p2[2], Clk, RAM_WE
  // PLD_RAM_OE pld_ram_oe_1: pin names not known; wires that end beside it: T[1], T[5], pld_s_ld_1_p2[1], T[3], pld_s_ld_1_p2[2], pld_s_ld_1_p2[5], RAM_OE
  // PLD_AR_LD pld_ar_ld_1: pin names not known; wires that end beside it: pld_s_ld_1_p2[6], Z_In, T[0], T[2], T[4], Clk, pld_s_ld_1_p2[1], AR_LD
  // PLD_PC_LD pld_pc_ld_1: pin names not known; wires that end beside it: pld_s_ld_1_p2[2], T[4], Clk, pld_s_ld_1_p2[5], pld_s_ld_1_p2[6], PC_LD
  // PLD_PC_INC pld_pc_inc_1: pin names not known; wires that end beside it: Z_In, T[3], Clk, pld_s_ld_1_p2[1], pld_s_ld_1_p2[2], pld_s_ld_1_p2[6], PC_INC
  // PLD_PC_BUS pld_pc_bus_1: pin names not known; wires that end beside it: Z_In, T[1], T[0], T[2], PC_BUS
  // PLD_DR_LD pld_dr_ld_1: pin names not known; wires that end beside it: T[1], T[3], T[5], pld_s_ld_1_p2[1], pld_s_ld_1_p2[2], pld_s_ld_1_p2[5], DR_LD
  // PLD_DR_BUS pld_dr_bus_1: pin names not known; wires that end beside it: pld_s_ld_1_p2[6], Z_In, Clk, T[4], T[6], pld_s_ld_1_p2[1], pld_s_ld_1_p2[2], pld_s_ld_1_p2[5], DR_BUS
  // PLD_R_LD pld_r_ld_1: pin names not known; wires that end beside it: pld_s_ld_1_p2[6], Z_In, T[3], pld_s_ld_1_p2[3], Clk, R_LD
  // PLD_R_BUS pld_r_bus_1: pin names not known; wires that end beside it: T[3], pld_s_ld_1_p2[4], pld_s_ld_1_p2[8], pld_s_ld_1_p2[9], pld_s_ld_1_p2[12], R_BUS
  // PLD_ACC_LD pld_acc_ld_1: pin names not known; wires that end beside it: pld_s_ld_1_p2[13], T[3], pld_s_ld_1_p2[4], pld_s_ld_1_p2[8], pld_s_ld_1_p2[9], pld_s_ld_1_p2[10], pld_s_ld_1_p2[12], pld_s_ld_1_p2[13], pld_s_ld_1_p2[14], ACC_LD
  // PLD_ACC_CLR pld_acc_clr_1: pin names not known; wires that end beside it: pld_s_ld_1_p2[15], T[6], pld_s_ld_1_p2[1], Clk, T[3], pld_s_ld_1_p2[11], ACC_CLR
  // PLD_ACC_BUS pld_acc_bus_1: pin names not known; wires that end beside it: T[3], pld_s_ld_1_p2[3], pld_s_ld_1_p2[7], T[5], ACC_BUS
  // SBC_ALU_SEL0 sbc_alu_sel0_1: pin names not known; wires that end beside it: pld_s_ld_1_p2[2], pld_s_ld_1_p2[1], pld_s_ld_1_p2[4], pld_s_ld_1_p2[9], pld_s_ld_1_p2[13], ALU_S[0]
  // SBC_ALU_SEL1 sbc_alu_sel1_1: pin names not known; wires that end beside it: pld_s_ld_1_p2[15], pld_s_ld_1_p2[1], pld_s_ld_1_p2[4], pld_s_ld_1_p2[10], pld_s_ld_1_p2[14], ALU_S[1]
  // SBC_ALU_SEL2 sbc_alu_sel2_1: pin names not known; wires that end beside it: pld_s_ld_1_p2[15], pld_s_ld_1_p2[12], pld_s_ld_1_p2[13], pld_s_ld_1_p2[14], pld_s_ld_1_p2[15], ALU_S[2]
  // PLD_OUTR_LD pld_outr_ld_1: pin names not known; wires that end beside it: T[3], pld_s_ld_1_p2[7], Clk, OUTR_LD
  // Z_LD z_ld_1: pin names not known; wires that end beside it: Z_lDD
endmodule

module S_Reg (
  input  Clk,
  input  Data,
  input  Clear,
  input  Load,
  output D_Out
);

  // Onebit_reg onebit_reg_1: pin names not known; wires that end beside it: Clk, Data, Clear, Load, D_Out
endmodule
